# Fritzing sketch ArduinoFio_OpenLog_GPS_Sharp (saved by Fritzing 0.7.10b)
breadboards: 1

parts:
  Arduino1 = Arduino Fio
  U1 = Sharp Optical Dust Sensor - 6 pins [part_number=GP2Y1010AU0F package=THT]
  220_uF = Electrolytic Capacitor [capacitance=220µF package="100 mil [THT, electrolytic]"]
  150_Ω = Resistor [tolerance=±5% resistance=150 package=THT]
  Part1 = OpenLog  # not connected

nets:
  N1: Arduino1.A6, U1.Vo
  N2: Arduino1.GND, U1.LED-GND, U1.S-GND, 220_uF.-
  3V3: Arduino1.3V3, U1.Vcc, 150_Ω.Pin_0
  N3: Arduino1.D12, U1.LED
  N4: U1.V-LED, 220_uF.+, 150_Ω.Pin_1

custom parts:
  Sharp Optical Dust Sensor - 6 pins: Sharp Optical Dust Sensor with a 6-pin 1.5mm pitch header footprint.
