# Fritzing sketch aq6s (saved by Fritzing 0.8.7b)
circuit board: 8.53505cm x 6.99456cm
breadboards: 1

parts:
  Part1 = Arduino Fio (Funnel I/O)
  GPS1 = Adafruit Ultimate GPS Breakout
  BMP1 = BMP085 Breakout
  Part2 = OpenLog
  SHT_Sensor1 = SHT Sensor
  U1 = 74HC595 [package="DIP16 [THT]"]
  C1 = Electrolytic Capacitor [capacitance=1µF package="100 mil [THT, electrolytic]"]
  R1 = Resistor [tolerance=±5% resistance=220 package=THT]
  R2 = Resistor [tolerance=±5% resistance=220 package=THT]
  R3 = Resistor [tolerance=±5% resistance=220 package=THT]
  LED1 = LED - 5mm [color="Red (633nm)" package="5 mm [THT]"]
  LED2 = LED - 5mm [color="Blue (505nm)" package="5 mm [THT]"]
  LED3 = LED - 5mm [color="Green (565nm)" package="5 mm [THT]"]
  C2 = Electrolytic Capacitor [capacitance=0.22mF package="100 mil [THT, electrolytic]"]
  R4 = Resistor [tolerance=±5% resistance=150 package=THT]
  VCC1 = Battery
  Q1 = NPN-Transistor [package="TO92 [THT]"]
  R6 = Resistor [tolerance=±5% resistance=10k package=THT]
  R7 = Resistor [tolerance=±5% resistance=4.7k package=THT]
  5V_out1 = 5V regulator
  5V_out2 = 5V regulator
  Part3 = GSM
  S1 = Round Pushbutton
  R5 = Resistor [tolerance=±5% resistance=10k package=THT]
  D1 = Sharp Optical Dust Sensor - 6 pins [part_number=GP2Y1010AU0F package=THT]

nets:
  VCC: Part1.VCC, Part1.AREF, GPS1.VIN, BMP1.VIN, Part2.VCC, SHT_Sensor1.VCC1, SHT_Sensor1.VCC2, U1.MR, U1.VCC, C1.+, 5V_out2.VIN
  GND: Part1.GND, GPS1.GND, BMP1.GND, Part2.GND, SHT_Sensor1.GND1, SHT_Sensor1.GND2, U1.GND, U1.OE, C1.-, LED1.anode, LED2.anode, LED3.anode, C2.-, VCC1.-, Q1.E, R7.Pin_0, 5V_out1.GND, 5V_out2.GND, Part3.GND, D1.LED-GND, D1.S-GND
  N1: Part1.D2, GPS1.RX
  N2: Part1.D3_PWM, GPS1.TX
  N3: Part1.D5_PWM, R5.Pin_0
  N4: Part1.D6_PWM, Part2.TXO
  N5: Part1.D7, Part2.RXI
  N6: Part1.D8, Part2.DTR
  N7: Part1.D9_PWM, U1.SH_CP
  N8: Part1.D10_PWM/SS, U1.ST_CP
  N9: Part1.D11_PWM/MOSI, SHT_Sensor1.DATA
  N10: Part1.D12/MISO, D1.LED
  N11: Part1.D13/SCK, SHT_Sensor1.SCK
  N12: Part1.A1, R6.Pin_0, R7.Pin_1
  N13: Part1.A2, U1.DS
  N14: Part1.A4/SDA, BMP1.SCL
  N15: Part1.A5/SCL, BMP1.SDA
  N16: Part1.A6, D1.Vo
  N17: Part1.A7, Part3.TP1
  N18: U1.Q1, R3.Pin_0
  N19: U1.Q2, R2.Pin_0
  N20: U1.Q0, R1.Pin_0
  N21: R1.Pin_1, LED3.cathode
  N22: R2.Pin_1, LED1.cathode
  N23: R3.Pin_1, LED2.cathode
  N24: C2.+, R4.Pin_0, D1.V-LED
  N25: R4.Pin_1, 5V_out2.VOUT, D1.Vcc
  N26: VCC1.+, S1.leg0
  N27: Q1.B, R5.Pin_1
  N28: Q1.C, Part3.HSW
  N29: R6.Pin_1, 5V_out1.VOUT, Part3.+5V
  N30: 5V_out1.VIN, S1.leg1

custom parts:
  BMP085 Breakout: A breakout for the BMP085 barometric pressure and temperature sensor
  5V regulator: The S7V7F5 switching step-up/step-down regulator efficiently produces 5 V from input voltages between 2.7 V and 11.8 V.
  GSM: Gas Sensor Module Rev A
  Sharp Optical Dust Sensor - 6 pins: Sharp Optical Dust Sensor with a 6-pin 1.5mm pitch header footprint.
